# Fritzing sketch button_panel (saved by Fritzing 0.9.3b)
circuit board: 8.46667cm x 5.64444cm
perfboards: 1

parts:
  R0 = Resistor [tolerance=±5% resistance=3.3k package=THT]
  R1 = Resistor [tolerance=±5% resistance=3.3k package=THT]
  R2 = Resistor [tolerance=±5% resistance=3.3k package=THT]
  R3 = Resistor [tolerance=±5% resistance=3.3k package=THT]
  R4 = Resistor [tolerance=±5% resistance=3.3k package=THT]
  R5 = Resistor [tolerance=±5% resistance=3.3k package=THT]
  R6 = Resistor [tolerance=±5% resistance=3.3k package=THT]
  R7 = Resistor [tolerance=±5% resistance=3.3k package=THT]
  R8 = Resistor [tolerance=±5% resistance=3.3k package=THT]
  R9 = Resistor [tolerance=±5% resistance=3.3k package=THT]
  R10 = Resistor [tolerance=±5% resistance=3.3k package=THT]
  R11 = Resistor [tolerance=±5% resistance=3.3k package=THT]
  P1 = Tactile Switch Buttons - 12mm Square [package=tactile-pth-12mm]
  P2 = Tactile Switch Buttons - 12mm Square [package=tactile-pth-12mm]
  P3 = Tactile Switch Buttons - 12mm Square [package=tactile-pth-12mm]
  P4 = Tactile Switch Buttons - 12mm Square [package=tactile-pth-12mm]
  P5 = Tactile Switch Buttons - 12mm Square [package=tactile-pth-12mm]
  P6 = Tactile Switch Buttons - 12mm Square [package=tactile-pth-12mm]
  P7 = Tactile Switch Buttons - 12mm Square [package=tactile-pth-12mm]
  P8 = Tactile Switch Buttons - 12mm Square [package=tactile-pth-12mm]
  P9 = Tactile Switch Buttons - 12mm Square [package=tactile-pth-12mm]
  P10 = Tactile Switch Buttons - 12mm Square [package=tactile-pth-12mm]
  J1 = female pin header, 6 pins [form="♀ (female)"]
  S1 = Toggle Switch [package=THT]
  LED1 = LED - 5mm [color="Red (633nm)" package="5 mm [THT]"]

nets:
  5V: R0.Pin_0, J1.pin1
  N1: R0.Pin_1, R1.Pin_0, P1.1, P1.3, P2.1, P2.3, P3.1, P3.3, P4.1, P4.3, P5.1, P5.3
  N2: R1.Pin_1, R2.Pin_0, P5.2, P5.4
  N3: R2.Pin_1, R3.Pin_0, P4.2, P4.4
  N4: R3.Pin_1, R4.Pin_0, P3.2, P3.4
  N5: R4.Pin_1, R5.Pin_0, P2.2, P2.4
  N6: R5.Pin_1, R6.Pin_1, P1.2, P1.4, P10.2, P10.4, J1.pin2
  N7: R6.Pin_0, R7.Pin_1, P9.2, P9.4
  N8: R7.Pin_0, R8.Pin_1, P8.2, P8.4
  N9: R8.Pin_0, R9.Pin_1, P7.2, P7.4
  N10: R9.Pin_0, R10.Pin_1, P6.2, P6.4
  N11: R10.Pin_0, R11.Pin_1, P6.1, P6.3, P7.1, P7.3, P8.1, P8.3, P9.1, P9.3, P10.1, P10.3
  N12: R11.Pin_0, J1.pin3
  N13: J1.pin4, S1.COM
  N14: J1.pin5, LED1.anode
  GND: S1.L2

custom parts:
  Tactile Switch Buttons - 12mm Square: Medium-sized clicky momentary switches are standard input "buttons" on electronic projects. These work best in a PCB but can be used on a solderless breadboard as shown in this tutorial. The pins are normally open (disconnected) and when the button is pressed they are momentarily closed. They come in a pack of 10, they're pretty handy so you'll want to keep them around. You can find an EAGLE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
