# Fritzing sketch ir_remote_breadboard (saved by Fritzing 0.9.3b)
breadboards: 1

parts:
  Часть1 = Arduino Nano (Rev3.0) (ICSP)
  S1 = Pushbutton [package="[SMD]"]
  R1 = Resistor [tolerance=±5% resistance=10k package=THT]
  IR1 = TSOP312.., 314.. [package=THT]

nets:
  N1: Часть1.D11/MOSI, IR1.Data
  N2: Часть1.D12/MISO, S1.Pin_1, S1.Pin_2, R1.Pin_0
  GND: Часть1.GND, R1.Pin_1, IR1.GND
  N3: Часть1.5V, S1.Pin_3, S1.Pin_4, IR1.Vs
